// Digital circuit ffjk.dig as structural Verilog
module ffjk (
  input  J,
  input  CK,
  input  K,
  input  pr,
  input  clr,
  output Q,
  output Q_2
);

  wire nand_1_out, nand_2_out;

  nand nand_1 (nand_1_out, Q_2, J, CK, clr);
  nand nand_2 (nand_2_out, pr, CK, K, Q);
  nand nand_3 (Q, pr, nand_1_out, Q_2);
  nand nand_4 (Q_2, Q, nand_2_out, clr);
endmodule
