// Digital circuit main.dig as structural Verilog
module main (
  input  CLOCK
);

  wire CLEAR_out, decoder_1_a0, decoder_1_a1, decoder_1_b0, decoder_1_b1, decoder_1_c0, decoder_1_c1,
       decoder_1_d0, decoder_1_d1, decoder_1_e0, decoder_1_e1, decoder_1_f0, decoder_1_f1, decoder_1_g0,
       decoder_1_g1, decoder_2_a0, decoder_2_a1, decoder_2_b0, decoder_2_b1, decoder_2_c0, decoder_2_c1,
       decoder_2_d0, decoder_2_d1, decoder_2_e0, decoder_2_e1, decoder_2_f0, decoder_2_f1, decoder_2_g0,
       decoder_2_g1, decoder_3_a0, decoder_3_a1, decoder_3_b0, decoder_3_b1, decoder_3_c0, decoder_3_c1,
       decoder_3_d0, decoder_3_d1, decoder_3_e0, decoder_3_e1, decoder_3_f0, decoder_3_f1, decoder_3_g0,
       decoder_3_g1, mod12_1_b0, mod12_1_b1, mod12_1_b2, mod12_1_b3, mod12_1_b4, mod12_1_o, mod60_1_p1,
       mod60_1_p2, mod60_1_p3, mod60_1_p4, mod60_1_p5, mod60_1_p7, mod60_1_p8, mod60_1_p9, mod60_2_p2,
       mod60_2_p3, mod60_2_p4, mod60_2_p5, mod60_2_p7, mod60_2_p9, or_1_out;

  Seven_Seg seven_seg_1 (
    .a(decoder_1_a1), .b(decoder_1_b1), .c(decoder_1_c1), .d(decoder_1_d1), .e(decoder_1_e1),
    .f(decoder_1_f1), .g(decoder_1_g1), .dp(1'b0));
  Seven_Seg seven_seg_2 (
    .a(decoder_1_a0), .b(decoder_1_b0), .c(decoder_1_c0), .d(decoder_1_d0), .e(decoder_1_e0),
    .f(decoder_1_f0), .g(decoder_1_g0), .dp(1'b0));
  Button CLEAR (.out(CLEAR_out));
  or or_1 (or_1_out, CLEAR_out, mod12_1_o);
  decoder decoder_1 (
    .i5(1'b0), .i4(mod12_1_b4), .i3(mod12_1_b3), .i2(mod12_1_b2), .i1(mod12_1_b1), .i0(mod12_1_b0),
    .a1(decoder_1_a1), .b1(decoder_1_b1), .c1(decoder_1_c1), .d1(decoder_1_d1), .e1(decoder_1_e1),
    .f1(decoder_1_f1), .g1(decoder_1_g1), .a0(decoder_1_a0), .b0(decoder_1_b0), .c0(decoder_1_c0),
    .d0(decoder_1_d0), .e0(decoder_1_e0), .f0(decoder_1_f0), .g0(decoder_1_g0));
  mod12 mod12_1 (
    .CK(mod60_1_p1), .CL(or_1_out), .B0(mod12_1_b0), .B1(mod12_1_b1), .B2(mod12_1_b2), .B3(mod12_1_b3),
    .B4(mod12_1_b4), .O(mod12_1_o));
  Seven_Seg seven_seg_3 (
    .a(decoder_2_a1), .b(decoder_2_b1), .c(decoder_2_c1), .d(decoder_2_d1), .e(decoder_2_e1),
    .f(decoder_2_f1), .g(decoder_2_g1), .dp(1'b0));
  Seven_Seg seven_seg_4 (
    .a(decoder_2_a0), .b(decoder_2_b0), .c(decoder_2_c0), .d(decoder_2_d0), .e(decoder_2_e0),
    .f(decoder_2_f0), .g(decoder_2_g0), .dp(1'b0));
  decoder decoder_2 (
    .i5(mod60_1_p2), .i4(mod60_1_p3), .i3(mod60_1_p4), .i2(mod60_1_p5), .i1(mod60_1_p7), .i0(mod60_1_p9),
    .a1(decoder_2_a1), .b1(decoder_2_b1), .c1(decoder_2_c1), .d1(decoder_2_d1), .e1(decoder_2_e1),
    .f1(decoder_2_f1), .g1(decoder_2_g1), .a0(decoder_2_a0), .b0(decoder_2_b0), .c0(decoder_2_c0),
    .d0(decoder_2_d0), .e0(decoder_2_e0), .f0(decoder_2_f0), .g0(decoder_2_g0));
  // mod60 mod60_1: pin names not known; wires that end beside it: mod60_1_p1, mod60_1_p2, mod60_1_p3, mod60_1_p4, mod60_1_p5, or_1_out, mod60_1_p7, mod60_1_p8, mod60_1_p9
  Seven_Seg seven_seg_5 (
    .a(decoder_3_a1), .b(decoder_3_b1), .c(decoder_3_c1), .d(decoder_3_d1), .e(decoder_3_e1),
    .f(decoder_3_f1), .g(decoder_3_g1), .dp(1'b0));
  Seven_Seg seven_seg_6 (
    .a(decoder_3_a0), .b(decoder_3_b0), .c(decoder_3_c0), .d(decoder_3_d0), .e(decoder_3_e0),
    .f(decoder_3_f0), .g(decoder_3_g0), .dp(1'b0));
  decoder decoder_3 (
    .i5(mod60_2_p2), .i4(mod60_2_p3), .i3(mod60_2_p4), .i2(mod60_2_p5), .i1(mod60_2_p7), .i0(mod60_2_p9),
    .a1(decoder_3_a1), .b1(decoder_3_b1), .c1(decoder_3_c1), .d1(decoder_3_d1), .e1(decoder_3_e1),
    .f1(decoder_3_f1), .g1(decoder_3_g1), .a0(decoder_3_a0), .b0(decoder_3_b0), .c0(decoder_3_c0),
    .d0(decoder_3_d0), .e0(decoder_3_e0), .f0(decoder_3_f0), .g0(decoder_3_g0));
  // mod60 mod60_2: pin names not known; wires that end beside it: mod60_1_p8, mod60_2_p2, mod60_2_p3, mod60_2_p4, mod60_2_p5, or_1_out, mod60_2_p7, CLOCK, mod60_2_p9
endmodule
