// Digital circuit mod10.dig as structural Verilog
module mod10 (
  input  CK,
  input  CL,
  output B0,
  output B1,
  output B2,
  output B3,
  output O
);

  wire jk_ff_as_1_nq, jk_ff_as_2_nq, jk_ff_as_3_nq, not_1_out, not_2_out, or_1_out;

  or or_1 (or_1_out, CL, O);
  JK_FF_AS jk_ff_as_1 (.Set(1'b0), .J(1'b1), .C(CK), .K(1'b1), .Clr(or_1_out), .Q(B0), .nQ(jk_ff_as_1_nq));
  not not_1 (not_1_out, B0);
  and and_1 (O, B3, not_2_out, B1, not_1_out);
  JK_FF_AS jk_ff_as_2 (.Set(1'b0), .J(1'b1), .C(jk_ff_as_1_nq), .K(1'b1), .Clr(or_1_out), .Q(B1), .nQ(jk_ff_as_2_nq));
  JK_FF_AS jk_ff_as_3 (.Set(1'b0), .J(1'b1), .C(jk_ff_as_2_nq), .K(1'b1), .Clr(or_1_out), .Q(B2), .nQ(jk_ff_as_3_nq));
  JK_FF_AS jk_ff_as_4 (.Set(1'b0), .J(1'b1), .C(jk_ff_as_3_nq), .K(1'b1), .Clr(or_1_out), .Q(B3));  // open: nQ
  not not_2 (not_2_out, B2);
endmodule
