// Digital circuit mod12v2.dig as structural Verilog
module mod12v2 (
  input  CK,
  input  CL,
  output U0,
  output U1,
  output U2,
  output U3,
  output D0
);

  wire and_1_out, mod10_1_o, not_1_out, not_2_out, or_1_out;

  or or_1 (or_1_out, and_1_out, CL);
  mod10 mod10_1 (.CK(CK), .CL(or_1_out), .B0(U0), .B1(U1), .B2(U2), .B3(U3), .O(mod10_1_o));
  and and_1 (and_1_out, U0, U1, D0, not_1_out, not_2_out);
  not not_1 (not_1_out, U2);
  JK_FF_AS jk_ff_as_1 (.Set(1'b0), .J(1'b1), .C(mod10_1_o), .K(1'b1), .Clr(or_1_out), .Q(D0));  // open: nQ
  not not_2 (not_2_out, U3);
endmodule
