// Digital circuit mod60.dig as structural Verilog
module mod60 (
  input  clk,
  output B0,
  output B1,
  output B2,
  output B3,
  output B4,
  output B5
);

  wire ffjk_1_q_2, ffjk_2_q_2, ffjk_3_q_2, ffjk_4_q_2, ffjk_5_q_2, nand_1_out, not_1_out, not_2_out;

  ffjk ffjk_1 (.J(1'b1), .CK(clk), .K(1'b1), .pr(1'b1), .clr(nand_1_out), .Q(B0), .Q_2(ffjk_1_q_2));
  nand nand_1 (nand_1_out, not_1_out, not_2_out, B2, B3, B4, B5);
  not not_1 (not_1_out, B0);
  ffjk ffjk_2 (.J(1'b1), .CK(ffjk_1_q_2), .K(1'b1), .pr(1'b1), .clr(nand_1_out), .Q(B1), .Q_2(ffjk_2_q_2));
  ffjk ffjk_3 (.J(1'b1), .CK(ffjk_2_q_2), .K(1'b1), .pr(1'b1), .clr(nand_1_out), .Q(B2), .Q_2(ffjk_3_q_2));
  not not_2 (not_2_out, B1);
  ffjk ffjk_4 (.J(1'b1), .CK(ffjk_3_q_2), .K(1'b1), .pr(1'b1), .clr(nand_1_out), .Q(B3), .Q_2(ffjk_4_q_2));
  ffjk ffjk_5 (.J(1'b1), .CK(ffjk_4_q_2), .K(1'b1), .pr(1'b1), .clr(nand_1_out), .Q(B4), .Q_2(ffjk_5_q_2));
  ffjk ffjk_6 (.J(1'b1), .CK(ffjk_5_q_2), .K(1'b1), .pr(1'b1), .clr(nand_1_out), .Q(B5));  // open: Q_2
endmodule
