// Digital circuit mod60v2.dig as structural Verilog
module mod60v2 (
  input  CL,
  input  CK,
  output O,
  output U0,
  output U1,
  output U2,
  output D0,
  output D1,
  output D2,
  output U3
);

  wire mod10_1_o;

  mod10 mod10_1 (.CK(CK), .CL(CL), .B0(U0), .B1(U1), .B2(U2), .B3(U3), .O(mod10_1_o));
  mod_5 mod_5_1 (.CK(mod10_1_o), .CL(CL), .B0(D0), .B1(D1), .B2(D2), .O(O));
endmodule
