// Digital circuit relogiov2.dlg.dig as structural Verilog
module relogiov2_dlg (
  input  CK
);

  wire and_1_out, button_1_out, button_2_out, button_3_out, button_4_out, decoderv2_1_a, decoderv2_1_b,
       decoderv2_1_c, decoderv2_1_d, decoderv2_1_e, decoderv2_1_f, decoderv2_1_g, decoderv2_2_a,
       decoderv2_2_b, decoderv2_2_c, decoderv2_2_d, decoderv2_2_e, decoderv2_2_f, decoderv2_2_g,
       decoderv2_3_a, decoderv2_3_b, decoderv2_3_c, decoderv2_3_d, decoderv2_3_e, decoderv2_3_f,
       decoderv2_3_g, decoderv2_4_a, decoderv2_4_b, decoderv2_4_c, decoderv2_4_d, decoderv2_4_e,
       decoderv2_4_f, decoderv2_4_g, decoderv2_5_a, decoderv2_5_b, decoderv2_5_c, decoderv2_5_d,
       decoderv2_5_e, decoderv2_5_f, decoderv2_5_g, decoderv2_6_a, decoderv2_6_b, decoderv2_6_c,
       decoderv2_6_d, decoderv2_6_e, decoderv2_6_f, decoderv2_6_g, jk_ff_1_q, mod12v2_1_d0, mod12v2_1_u0,
       mod12v2_1_u1, mod12v2_1_u2, mod12v2_1_u3, mod60v2_1_d0, mod60v2_1_d1, mod60v2_1_d2, mod60v2_1_o,
       mod60v2_1_u0, mod60v2_1_u1, mod60v2_1_u2, mod60v2_1_u3, mod60v2_2_d0, mod60v2_2_d1, mod60v2_2_d2,
       mod60v2_2_o, mod60v2_2_u0, mod60v2_2_u1, mod60v2_2_u2, mod60v2_2_u3, or_1_out, or_2_out;

  mod12v2 mod12v2_1 (
    .CK(or_1_out), .CL(button_4_out), .U0(mod12v2_1_u0), .U1(mod12v2_1_u1), .U2(mod12v2_1_u2),
    .U3(mod12v2_1_u3), .D0(mod12v2_1_d0));
  decoderv2 decoderv2_1 (
    .D3(mod12v2_1_u3), .D2(mod12v2_1_u2), .D1(mod12v2_1_u1), .D0(mod12v2_1_u0), .a(decoderv2_1_a),
    .b(decoderv2_1_b), .c(decoderv2_1_c), .d(decoderv2_1_d), .e(decoderv2_1_e), .f(decoderv2_1_f),
    .g(decoderv2_1_g));
  decoderv2 decoderv2_2 (
    .D3(1'b0), .D2(1'b0), .D1(1'b0), .D0(mod12v2_1_d0), .a(decoderv2_2_a), .b(decoderv2_2_b),
    .c(decoderv2_2_c), .d(decoderv2_2_d), .e(decoderv2_2_e), .f(decoderv2_2_f), .g(decoderv2_2_g));
  Seven_Seg seven_seg_1 (
    .a(decoderv2_2_a), .b(decoderv2_2_b), .c(decoderv2_2_c), .d(decoderv2_2_d), .e(decoderv2_2_e),
    .f(decoderv2_2_f), .g(decoderv2_2_g), .dp(1'b0));
  Seven_Seg seven_seg_2 (
    .a(decoderv2_1_a), .b(decoderv2_1_b), .c(decoderv2_1_c), .d(decoderv2_1_d), .e(decoderv2_1_e),
    .f(decoderv2_1_f), .g(decoderv2_1_g), .dp(1'b0));
  or or_1 (or_1_out, button_1_out, mod60v2_1_o);
  mod60v2 mod60v2_1 (
    .CL(button_4_out), .CK(or_2_out), .O(mod60v2_1_o), .U0(mod60v2_1_u0), .U1(mod60v2_1_u1),
    .U2(mod60v2_1_u2), .D0(mod60v2_1_d0), .D1(mod60v2_1_d1), .D2(mod60v2_1_d2), .U3(mod60v2_1_u3));
  Button button_1 (.out(button_1_out));
  decoderv2 decoderv2_3 (
    .D3(mod60v2_1_u3), .D2(mod60v2_1_u2), .D1(mod60v2_1_u1), .D0(mod60v2_1_u0), .a(decoderv2_3_a),
    .b(decoderv2_3_b), .c(decoderv2_3_c), .d(decoderv2_3_d), .e(decoderv2_3_e), .f(decoderv2_3_f),
    .g(decoderv2_3_g));
  decoderv2 decoderv2_4 (
    .D3(1'b0), .D2(mod60v2_1_d2), .D1(mod60v2_1_d1), .D0(mod60v2_1_d0), .a(decoderv2_4_a), .b(decoderv2_4_b),
    .c(decoderv2_4_c), .d(decoderv2_4_d), .e(decoderv2_4_e), .f(decoderv2_4_f), .g(decoderv2_4_g));
  or or_2 (or_2_out, button_2_out, mod60v2_2_o);
  Seven_Seg seven_seg_3 (
    .a(decoderv2_4_a), .b(decoderv2_4_b), .c(decoderv2_4_c), .d(decoderv2_4_d), .e(decoderv2_4_e),
    .f(decoderv2_4_f), .g(decoderv2_4_g), .dp(1'b0));
  Button button_2 (.out(button_2_out));
  Seven_Seg seven_seg_4 (
    .a(decoderv2_3_a), .b(decoderv2_3_b), .c(decoderv2_3_c), .d(decoderv2_3_d), .e(decoderv2_3_e),
    .f(decoderv2_3_f), .g(decoderv2_3_g), .dp(1'b0));
  mod60v2 mod60v2_2 (
    .CL(button_4_out), .CK(and_1_out), .O(mod60v2_2_o), .U0(mod60v2_2_u0), .U1(mod60v2_2_u1),
    .U2(mod60v2_2_u2), .D0(mod60v2_2_d0), .D1(mod60v2_2_d1), .D2(mod60v2_2_d2), .U3(mod60v2_2_u3));
  and and_1 (and_1_out, CK, jk_ff_1_q);
  JK_FF jk_ff_1 (.J(1'b1), .C(button_3_out), .K(1'b1), .Q(jk_ff_1_q));  // open: nQ
  Button button_3 (.out(button_3_out));
  decoderv2 decoderv2_5 (
    .D3(mod60v2_2_u3), .D2(mod60v2_2_u2), .D1(mod60v2_2_u1), .D0(mod60v2_2_u0), .a(decoderv2_5_a),
    .b(decoderv2_5_b), .c(decoderv2_5_c), .d(decoderv2_5_d), .e(decoderv2_5_e), .f(decoderv2_5_f),
    .g(decoderv2_5_g));
  decoderv2 decoderv2_6 (
    .D3(1'b0), .D2(mod60v2_2_d2), .D1(mod60v2_2_d1), .D0(mod60v2_2_d0), .a(decoderv2_6_a), .b(decoderv2_6_b),
    .c(decoderv2_6_c), .d(decoderv2_6_d), .e(decoderv2_6_e), .f(decoderv2_6_f), .g(decoderv2_6_g));
  Seven_Seg seven_seg_5 (
    .a(decoderv2_6_a), .b(decoderv2_6_b), .c(decoderv2_6_c), .d(decoderv2_6_d), .e(decoderv2_6_e),
    .f(decoderv2_6_f), .g(decoderv2_6_g), .dp(1'b0));
  Button button_4 (.out(button_4_out));
  Seven_Seg seven_seg_6 (
    .a(decoderv2_5_a), .b(decoderv2_5_b), .c(decoderv2_5_c), .d(decoderv2_5_d), .e(decoderv2_5_e),
    .f(decoderv2_5_f), .g(decoderv2_5_g), .dp(1'b0));

  // Notes on the sheet:
  //   CK: Hz: 3600
endmodule
